// Logisim project 0 to 90 counter.circ as structural Verilog: 10 circuits, main circuit main
module main (
  input  C,
  input  Reset,
  output A0,
  output A1,
  output A2,
  output A3,
  output Clk
);

  wire d_ff_1_qn, d_ff_2_qn, d_ff_3_qn, d_ff_4_qn, or_1_out;

  or or_1 (or_1_out, Reset, Clk);
  D_Flip_Flop d_ff_1 (.clk(C), .D(d_ff_1_qn), .Q(A0), .Qn(d_ff_1_qn), .reset(or_1_out));  // open: preset, en
  D_Flip_Flop d_ff_2 (.clk(d_ff_1_qn), .D(d_ff_2_qn), .Q(A1), .Qn(d_ff_2_qn), .reset(or_1_out));  // open: preset, en
  D_Flip_Flop d_ff_3 (.clk(d_ff_2_qn), .D(d_ff_3_qn), .Q(A2), .Qn(d_ff_3_qn), .reset(or_1_out));  // open: preset, en
  D_Flip_Flop d_ff_4 (.clk(d_ff_3_qn), .D(d_ff_4_qn), .Q(A3), .Qn(d_ff_4_qn), .reset(or_1_out));  // open: preset, en
  and and_1 (Clk, A3, A1);
endmodule

module ssd (
  input  in_1,
  input  in_2,
  input  in_3,
  input  in_4,
  output out_5,
  output out_6,
  output out_7,
  output out_8,
  output out_9,
  output out_10,
  output out_11
);

  wire n4_to16_decoder_1_out_5, n4_to16_decoder_1_out_6, n4_to16_decoder_1_out_7, n4_to16_decoder_1_out_8,
       n4_to16_decoder_1_out_9, n4_to16_decoder_1_out_10, n4_to16_decoder_1_out_11, n4_to16_decoder_1_out_12,
       n4_to16_decoder_1_out_13, n4_to16_decoder_1_out_14;

  _4_to16_decoder u_4_to16_decoder_1 (
    .in_1(in_4), .in_2(in_3), .in_3(in_2), .in_4(in_1), .out_5(n4_to16_decoder_1_out_5),
    .out_6(n4_to16_decoder_1_out_6), .out_7(n4_to16_decoder_1_out_7), .out_8(n4_to16_decoder_1_out_8),
    .out_9(n4_to16_decoder_1_out_9), .out_10(n4_to16_decoder_1_out_10), .out_11(n4_to16_decoder_1_out_11),
    .out_12(n4_to16_decoder_1_out_12), .out_13(n4_to16_decoder_1_out_13), .out_14(n4_to16_decoder_1_out_14));  // open: out_15, out_16, out_17, out_18, out_19, out_20
  or or_1 (out_5, n4_to16_decoder_1_out_5, n4_to16_decoder_1_out_8, n4_to16_decoder_1_out_7, n4_to16_decoder_1_out_10, n4_to16_decoder_1_out_11, n4_to16_decoder_1_out_12, n4_to16_decoder_1_out_13, n4_to16_decoder_1_out_14);
  or or_2 (out_6, n4_to16_decoder_1_out_8, n4_to16_decoder_1_out_5, n4_to16_decoder_1_out_6, n4_to16_decoder_1_out_7, n4_to16_decoder_1_out_9, n4_to16_decoder_1_out_12, n4_to16_decoder_1_out_13, n4_to16_decoder_1_out_14);
  or or_3 (out_7, n4_to16_decoder_1_out_5, n4_to16_decoder_1_out_6, n4_to16_decoder_1_out_8, n4_to16_decoder_1_out_9, n4_to16_decoder_1_out_10, n4_to16_decoder_1_out_11, n4_to16_decoder_1_out_12, n4_to16_decoder_1_out_13, n4_to16_decoder_1_out_14);
  or or_4 (out_8, n4_to16_decoder_1_out_5, n4_to16_decoder_1_out_7, n4_to16_decoder_1_out_8, n4_to16_decoder_1_out_10, n4_to16_decoder_1_out_11, n4_to16_decoder_1_out_13, n4_to16_decoder_1_out_14);
  or or_5 (out_9, n4_to16_decoder_1_out_5, n4_to16_decoder_1_out_7, n4_to16_decoder_1_out_11, n4_to16_decoder_1_out_13);
  or or_6 (out_10, n4_to16_decoder_1_out_5, n4_to16_decoder_1_out_9, n4_to16_decoder_1_out_10, n4_to16_decoder_1_out_11, n4_to16_decoder_1_out_13, n4_to16_decoder_1_out_14);
  or or_7 (out_11, n4_to16_decoder_1_out_7, n4_to16_decoder_1_out_8, n4_to16_decoder_1_out_9, n4_to16_decoder_1_out_10, n4_to16_decoder_1_out_11, n4_to16_decoder_1_out_13, n4_to16_decoder_1_out_14);
endmodule

module display (
  input  in_1
);

  wire and_1_out, clock_1_out, main_1_a0, main_1_a1, main_1_a2, main_2_clk, or_1_out, ssd_1_out_5,
       ssd_1_out_6, ssd_1_out_7, ssd_1_out_8, ssd_1_out_9, ssd_1_out_10, ssd_1_out_11, ssd_2_p1, ssd_2_p2,
       ssd_2_p3, ssd_2_p4, ssd_2_p5, ssd_2_p7, ssd_2_p8, ssd_2_p9, ssd_2_p10, ssd_2_p11;

  or or_1 (or_1_out, in_1, and_1_out);
  main main_1 (
    .C(main_2_clk), .Reset(or_1_out), .A0(main_1_a0), .A1(main_1_a1), .A2(main_1_a2), .A3(main_1_a0));  // open: Clk
  and and_1 (and_1_out, main_1_a0, ssd_2_p11, main_1_a0);
  ssd ssd_1 (
    .in_2(main_1_a1), .in_3(main_1_a2), .in_4(main_1_a0), .out_5(ssd_1_out_5), .out_6(ssd_1_out_6),
    .out_7(ssd_1_out_7), .out_8(ssd_1_out_8), .out_9(ssd_1_out_9), .out_10(ssd_1_out_10),
    .out_11(ssd_1_out_11));  // open: in_1
  _7_Segment_Display u_7_segment_display_1 (
    .g(ssd_1_out_9), .f(ssd_1_out_8), .a(ssd_1_out_10), .b(ssd_1_out_11), .e(ssd_1_out_7), .d(ssd_1_out_6),
    .c(ssd_1_out_5));  // open: dp
  _7_Segment_Display u_7_segment_display_2 (
    .g(ssd_2_p1), .f(ssd_2_p2), .a(ssd_2_p7), .b(ssd_2_p4), .e(ssd_2_p3), .d(ssd_2_p4), .c(ssd_2_p5));  // open: dp
  // ssd ssd_2: pin names not known; wires that end beside it: ssd_2_p1, ssd_2_p2, ssd_2_p3, ssd_2_p4, ssd_2_p5, ssd_2_p4, ssd_2_p7, ssd_2_p8, ssd_2_p9, ssd_2_p10, ssd_2_p11
  main main_2 (
    .C(clock_1_out), .Clk(main_2_clk), .Reset(or_1_out), .A0(ssd_2_p11), .A1(ssd_2_p10), .A2(ssd_2_p9),
    .A3(ssd_2_p8));
  Clock clock_1 (.out(clock_1_out));
endmodule

module _4_to16_decoder (
  input  in_1,
  input  in_2,
  input  in_3,
  input  in_4,
  output out_5,
  output out_6,
  output out_7,
  output out_8,
  output out_9,
  output out_10,
  output out_11,
  output out_12,
  output out_13,
  output out_14,
  output out_15,
  output out_16,
  output out_17,
  output out_18,
  output out_19,
  output out_20
);

  wire not_1_out, not_2_out, not_3_out, not_4_out, not_5_out, not_6_out, not_7_out, not_8_out;

  not not_1 (not_1_out, in_4);
  not not_2 (not_2_out, in_4);
  not not_3 (not_3_out, in_4);
  not not_4 (not_4_out, in_4);
  not not_5 (not_5_out, in_4);
  not not_6 (not_6_out, in_4);
  not not_7 (not_7_out, in_4);
  not not_8 (not_8_out, in_4);
  and and_1 (out_5, ~in_1, ~in_2, ~in_3, not_1_out);  // AND_Gate
  and and_2 (out_6, ~in_1, ~in_2, ~in_3, in_4);  // AND_Gate
  and and_3 (out_7, ~in_1, ~in_2, in_3, not_2_out);  // AND_Gate
  and and_4 (out_8, ~in_1, ~in_2, in_3, in_4);  // AND_Gate
  and and_5 (out_9, ~in_1, in_2, ~in_3, not_3_out);  // AND_Gate
  and and_6 (out_10, ~in_1, in_2, ~in_3, in_4);  // AND_Gate
  and and_7 (out_11, ~in_1, in_2, in_3, not_4_out);  // AND_Gate
  and and_8 (out_12, ~in_1, in_2, in_3, in_4);  // AND_Gate
  and and_9 (out_13, in_1, ~in_2, ~in_3, not_5_out);  // AND_Gate
  and and_10 (out_14, in_1, ~in_2, ~in_3, in_4);  // AND_Gate
  and and_11 (out_15, in_1, ~in_2, in_3, not_6_out);  // AND_Gate
  and and_12 (out_16, in_1, ~in_2, in_3, in_4);  // AND_Gate
  and and_13 (out_17, in_1, in_2, ~in_3, not_7_out);  // AND_Gate
  and and_14 (out_18, in_1, in_2, ~in_3, in_4);  // AND_Gate
  and and_15 (out_19, in_1, in_2, in_3, not_8_out);
  and and_16 (out_20, in_1, in_2, in_3, in_4);
endmodule

module display_breadboard (
  input  in_1,
  input  Reset
);

  wire andgate_74f08n_1_q1, andgate_74f08n_1_q4, dflipflop_1_out_11, dflipflop_1_out_12, dflipflop_1_out_13,
       dflipflop_1_out_14, dflipflop_2_out_11, dflipflop_2_out_12, dflipflop_2_out_13, dflipflop_2_out_14,
       dflipflop_3_out_11, dflipflop_3_out_12, dflipflop_3_out_13, dflipflop_4_out_11, dflipflop_4_out_12,
       dflipflop_4_out_13, dflipflop_4_out_14, or_gate_1_q1, or_gate_1_q3, ssd_1_out_5, ssd_1_out_6,
       ssd_1_out_7, ssd_1_out_8, ssd_1_out_9, ssd_1_out_10, ssd_1_out_11, ssd_2_out_5, ssd_2_out_6,
       ssd_2_out_7, ssd_2_out_8, ssd_2_out_9, ssd_2_out_10, ssd_2_out_11, undriven;

  ANDgate_74F08N andgate_74f08n_1 (
    .B4(dflipflop_3_out_12), .A4(dflipflop_4_out_11), .Q4(andgate_74f08n_1_q4), .A1(dflipflop_1_out_12),
    .B1(dflipflop_2_out_11), .Q1(andgate_74f08n_1_q1));  // open: B3, A3, Q3, A2, B2, Q2
  Dflipflop dflipflop_1 (
    .in_1(dflipflop_1_out_14), .in_2(dflipflop_2_out_14), .in_3(dflipflop_1_out_13),
    .in_4(dflipflop_1_out_14), .Clear(or_gate_1_q1), .clear_2(or_gate_1_q1), .out_11(dflipflop_1_out_11),
    .out_12(dflipflop_1_out_12), .out_13(dflipflop_1_out_13), .out_14(dflipflop_1_out_14));  // open: PS, PS_2, E, E_2
  OR_gate or_gate_1 (
    ._1A(andgate_74f08n_1_q1), ._1B(Reset), .Q1(or_gate_1_q1), ._3A(in_1), ._3B(andgate_74f08n_1_q4),
    .Q3(or_gate_1_q3));  // open: _2A, _2B, Q2, _4A, _4B, Q4
  Dflipflop dflipflop_2 (
    .in_1(dflipflop_1_out_13), .in_2(undriven), .in_3(dflipflop_2_out_13), .in_4(dflipflop_2_out_14),
    .Clear(or_gate_1_q1), .clear_2(or_gate_1_q1), .out_11(dflipflop_2_out_11), .out_12(dflipflop_2_out_12),
    .out_13(dflipflop_2_out_13), .out_14(dflipflop_2_out_14));  // open: PS, PS_2, E, E_2
  Clock clock_1 ();  // open: out
  ssd ssd_1 (
    .in_1(dflipflop_4_out_12), .in_2(dflipflop_3_out_12), .in_3(dflipflop_3_out_11),
    .in_4(dflipflop_4_out_11), .out_5(ssd_1_out_5), .out_6(ssd_1_out_6), .out_7(ssd_1_out_7),
    .out_8(ssd_1_out_8), .out_9(ssd_1_out_9), .out_10(ssd_1_out_10), .out_11(ssd_1_out_11));
  ssd ssd_2 (
    .in_1(dflipflop_2_out_12), .in_2(dflipflop_1_out_12), .in_3(dflipflop_1_out_11),
    .in_4(dflipflop_2_out_11), .out_5(ssd_2_out_5), .out_6(ssd_2_out_6), .out_7(ssd_2_out_7),
    .out_8(ssd_2_out_8), .out_9(ssd_2_out_9), .out_10(ssd_2_out_10), .out_11(ssd_2_out_11));
  Dflipflop dflipflop_3 (
    .in_1(dflipflop_3_out_11), .in_2(dflipflop_4_out_14), .in_3(dflipflop_3_out_13),
    .in_4(dflipflop_3_out_11), .Clear(or_gate_1_q3), .clear_2(or_gate_1_q3), .out_11(dflipflop_3_out_11),
    .out_12(dflipflop_3_out_12), .out_13(dflipflop_3_out_13), .out_14(dflipflop_3_out_11));  // open: PS, PS_2, E, E_2
  Dflipflop dflipflop_4 (
    .in_1(dflipflop_3_out_13), .in_2(andgate_74f08n_1_q1), .in_3(dflipflop_4_out_13),
    .in_4(dflipflop_4_out_14), .Clear(or_gate_1_q3), .clear_2(or_gate_1_q3), .out_11(dflipflop_4_out_11),
    .out_12(dflipflop_4_out_12), .out_13(dflipflop_4_out_13), .out_14(dflipflop_4_out_14));  // open: PS, PS_2, E, E_2
  _7_Segment_Display u_7_segment_display_1 (
    .g(ssd_2_out_11), .f(ssd_2_out_10), .a(ssd_2_out_5), .b(ssd_2_out_6), .e(ssd_2_out_9), .d(ssd_2_out_8),
    .c(ssd_2_out_7));  // open: dp
  _7_Segment_Display u_7_segment_display_2 (
    .g(ssd_1_out_8), .f(ssd_1_out_9), .a(ssd_1_out_7), .b(ssd_1_out_6), .e(ssd_1_out_10), .d(ssd_1_out_11),
    .c(ssd_1_out_5));  // open: dp
endmodule

module Dflipflop (
  input  in_1,
  input  in_2,
  input  in_3,
  input  in_4,
  input  Clear,
  input  PS,
  input  PS_2,
  input  clear_2,
  input  E,
  input  E_2,
  output out_11,
  output out_12,
  output out_13,
  output out_14
);

  wire undriven, undriven_2, undriven_3, undriven_4;

  D_Flip_Flop d_ff_1 (.clk(in_1), .D(in_3), .Q(out_11), .Qn(out_13), .preset(PS_2), .en(undriven), .reset(undriven_2));
  D_Flip_Flop d_ff_2 (.clk(in_2), .D(in_4), .Q(out_12), .Qn(out_14), .preset(PS), .en(undriven_3), .reset(undriven_4));
endmodule

module OR_gate (
  input  _1A,
  input  _3A,
  input  _1B,
  input  _3B,
  input  _2A,
  input  _4A,
  input  _2B,
  input  _4B,
  output Q3,
  output Q1,
  output Q4,
  output Q2
);

  or or_1 (Q1, _1B, _1A);
  or or_2 (Q2, _2B, _2A);
  or or_3 (Q3, _3A, _3B);
  or or_4 (Q4, _4A, _4B);
endmodule

module ANDgate_74F08N (
  input  B4,
  input  A4,
  input  B3,
  input  A3,
  input  A1,
  input  B1,
  input  A2,
  input  B2,
  output Q4,
  output Q3,
  output Q1,
  output Q2
);

  and and_1 (Q4, A4, B4);
  and and_2 (Q1, A1, B1);
  and and_3 (Q3, A3, B3);
  and and_4 (Q2, A2, B2);
endmodule

module notgate (
  input  in_1,
  input  in_2,
  input  in_3,
  input  in_4,
  input  in_5,
  input  in_6,
  output out_7,
  output out_8,
  output out_9,
  output out_10,
  output out_11,
  output out_12
);

  not not_1 (out_7, in_1);
  not not_2 (out_10, in_4);
  not not_3 (out_9, in_2);
  not not_4 (out_11, in_5);
  not not_5 (out_12, in_6);
  not not_6 (out_8, in_3);
endmodule

module abc (
  input  in_1
);

  wire andgate_74f08n_1_q4, clock_1_out, dflipflop_1_out_11, dflipflop_1_out_12, dflipflop_1_out_13,
       dflipflop_1_out_14, dflipflop_2_out_11, dflipflop_2_out_12, dflipflop_2_out_13, dflipflop_2_out_14,
       or_gate_1_q3, ssd_1_out_5, ssd_1_out_6, ssd_1_out_7, ssd_1_out_8, ssd_1_out_9, ssd_1_out_10,
       ssd_1_out_11;

  ANDgate_74F08N andgate_74f08n_1 (
    .B4(dflipflop_1_out_12), .A4(dflipflop_2_out_11), .Q4(andgate_74f08n_1_q4));  // open: B3, A3, Q3, A1, B1, Q1, A2, B2, Q2
  OR_gate or_gate_1 (
    ._3A(andgate_74f08n_1_q4), ._3B(in_1), .Q3(or_gate_1_q3));  // open: _1A, _1B, Q1, _2A, _2B, Q2, _4A, _4B, Q4
  ssd ssd_1 (
    .in_1(dflipflop_2_out_12), .in_2(dflipflop_1_out_12), .in_3(dflipflop_1_out_11),
    .in_4(dflipflop_2_out_11), .out_5(ssd_1_out_5), .out_6(ssd_1_out_6), .out_7(ssd_1_out_7),
    .out_8(ssd_1_out_8), .out_9(ssd_1_out_9), .out_10(ssd_1_out_10), .out_11(ssd_1_out_11));
  Dflipflop dflipflop_1 (
    .in_1(dflipflop_1_out_14), .in_2(dflipflop_2_out_14), .in_3(dflipflop_1_out_13),
    .in_4(dflipflop_1_out_14), .Clear(or_gate_1_q3), .clear_2(or_gate_1_q3), .out_11(dflipflop_1_out_11),
    .out_12(dflipflop_1_out_12), .out_13(dflipflop_1_out_13), .out_14(dflipflop_1_out_14));  // open: PS, PS_2, E, E_2
  Dflipflop dflipflop_2 (
    .in_1(dflipflop_1_out_13), .in_2(clock_1_out), .in_3(dflipflop_2_out_13), .in_4(dflipflop_2_out_14),
    .Clear(or_gate_1_q3), .clear_2(or_gate_1_q3), .out_11(dflipflop_2_out_11), .out_12(dflipflop_2_out_12),
    .out_13(dflipflop_2_out_13), .out_14(dflipflop_2_out_14));  // open: PS, PS_2, E, E_2
  _7_Segment_Display u_7_segment_display_1 (
    .g(ssd_1_out_8), .f(ssd_1_out_9), .a(ssd_1_out_7), .b(ssd_1_out_6), .e(ssd_1_out_10), .d(ssd_1_out_11),
    .c(ssd_1_out_5));  // open: dp
  Clock clock_1 (.out(clock_1_out));
endmodule
