// Logisim project Counter.circ as structural Verilog: 2 circuits, main circuit display
module _0_9_ssd (
  input  R,
  input  E,
  input  C,
  output A,
  output B,
  output C_2,
  output D,
  output E_2,
  output F,
  output G,
  output clk2
);

  wire and_2_out, and_3_out, and_4_out, and_5_out, and_6_out, and_7_out, and_8_out, and_9_out, and_10_out,
       and_11_out, and_12_out, d_ff_4_q, not_1_out, or_1_out, or_2_out, or_3_out, or_4_out, or_5_out,
       or_6_out, or_7_out;

  D_Flip_Flop d_ff_1 (.clk(C), .D(or_1_out), .Q(A), .preset(R), .en(E));  // open: Qn, reset
  D_Flip_Flop d_ff_2 (.clk(C), .D(or_3_out), .Q(C_2), .preset(R), .en(E));  // open: Qn, reset
  D_Flip_Flop d_ff_3 (.clk(C), .D(or_5_out), .Q(E_2), .preset(R), .en(E));  // open: Qn, reset
  D_Flip_Flop d_ff_4 (.clk(C), .D(not_1_out), .Q(d_ff_4_q), .Qn(G), .preset(R), .en(E));  // open: reset
  and and_1 (clk2, d_ff_4_q, E_2);
  not not_1 (not_1_out, or_7_out);
  or or_1 (or_1_out, and_2_out, ~C_2, and_3_out, and_4_out);  // OR_Gate
  or or_2 (or_2_out, and_2_out, and_4_out, and_10_out);
  D_Flip_Flop d_ff_5 (.clk(C), .D(or_4_out), .Q(B), .preset(R), .en(E));  // open: Qn, reset
  D_Flip_Flop d_ff_6 (.clk(C), .D(or_2_out), .Q(D), .preset(R), .en(E));  // open: Qn, reset
  D_Flip_Flop d_ff_7 (.clk(C), .D(or_6_out), .Q(F), .preset(R), .en(E));  // open: Qn, reset
  or or_3 (or_3_out, A, F);
  or or_4 (or_4_out, and_5_out, E_2, ~F);  // OR_Gate
  or or_5 (or_5_out, and_6_out, and_11_out);
  or or_6 (or_6_out, and_12_out, and_7_out, and_8_out);
  or or_7 (or_7_out, and_10_out, ~D, ~F, and_9_out);  // OR_Gate
  and and_2 (and_2_out, ~E_2, F);  // AND_Gate
  and and_3 (and_3_out, F, G);
  and and_4 (and_4_out, ~E_2, ~G);  // AND_Gate
  and and_5 (and_5_out, A, B);
  and and_6 (and_6_out, D, ~E_2, F);  // AND_Gate
  and and_7 (and_7_out, A, C_2, ~F);  // AND_Gate
  and and_8 (and_8_out, A, ~E_2);  // AND_Gate
  and and_9 (and_9_out, ~B, ~E_2);  // AND_Gate
  and and_10 (and_10_out, B, E_2, G);
  and and_11 (and_11_out, ~D, ~F);  // AND_Gate
  and and_12 (and_12_out, B, F, G);

  // Notes on the sheet:
  //   C
  //   C
endmodule

module display (
  input  PRESET,
  input  ENABLE
);

  wire and_1_out, clock_1_out, n0_9_ssd_1_a, n0_9_ssd_1_b, n0_9_ssd_1_c_2, n0_9_ssd_1_d, n0_9_ssd_1_e_2,
       n0_9_ssd_1_f, n0_9_ssd_1_g, n0_9_ssd_2_a, n0_9_ssd_2_b, n0_9_ssd_2_c_2, n0_9_ssd_2_clk2, n0_9_ssd_2_d,
       n0_9_ssd_2_e_2, n0_9_ssd_2_f, n0_9_ssd_2_g, or_1_out;

  or or_1 (or_1_out, PRESET, and_1_out);
  _0_9_ssd u_0_9_ssd_1 (
    .C(n0_9_ssd_2_clk2), .R(or_1_out), .E(ENABLE), .A(n0_9_ssd_1_a), .B(n0_9_ssd_1_b), .C_2(n0_9_ssd_1_c_2),
    .D(n0_9_ssd_1_d), .E_2(n0_9_ssd_1_e_2), .F(n0_9_ssd_1_f), .G(n0_9_ssd_1_g));  // open: clk2
  and and_1 (and_1_out, ~n0_9_ssd_1_e_2, n0_9_ssd_1_f, n0_9_ssd_1_a, n0_9_ssd_1_b, ~n0_9_ssd_2_a, ~n0_9_ssd_2_g);  // AND_Gate
  _7_Segment_Display u_7_segment_display_1 (
    .g(n0_9_ssd_1_g), .f(n0_9_ssd_1_f), .a(n0_9_ssd_1_a), .b(n0_9_ssd_1_b), .e(n0_9_ssd_1_e_2),
    .d(n0_9_ssd_1_d), .c(n0_9_ssd_1_c_2));  // open: dp
  _7_Segment_Display u_7_segment_display_2 (
    .g(n0_9_ssd_2_g), .f(n0_9_ssd_2_f), .a(n0_9_ssd_2_a), .b(n0_9_ssd_2_b), .e(n0_9_ssd_2_e_2),
    .d(n0_9_ssd_2_d), .c(n0_9_ssd_2_c_2));  // open: dp
  _0_9_ssd u_0_9_ssd_2 (
    .C(clock_1_out), .R(or_1_out), .E(ENABLE), .clk2(n0_9_ssd_2_clk2), .A(n0_9_ssd_2_a), .B(n0_9_ssd_2_b),
    .C_2(n0_9_ssd_2_c_2), .D(n0_9_ssd_2_d), .E_2(n0_9_ssd_2_e_2), .F(n0_9_ssd_2_f), .G(n0_9_ssd_2_g));
  Clock clock_1 (.out(clock_1_out));
endmodule
